# Fritzing sketch Plan_Plantare_432E (saved by Fritzing 0.9.3b)
circuit board: 41.1078cm x 20.7608cm
perfboards: 1

parts:
  R5 = Resistor [tolerance=±5% resistance=82 package=THT]
  D2 = Rectifier Diode [part_number=1N4148 package="300 mil [THT]"]
  R4 = Resistor [tolerance=±5% resistance=82 package=THT]
  LED2 = LED - 5mm [color="Red (633nm)" package="5 mm [THT]"]
  C1 = Ceramic Capacitor [capacitance=100nF package="100 mil [THT, multilayer]"]
  T9 = PNP-Transistor [package="TO92 [THT]"]
  LED1 = LED - 5mm [color="Red (633nm)" package="5 mm [THT]"]
  T4 = PNP-Transistor [part_number=BC556B package="TO92 [THT]"]
  C5 = Ceramic Capacitor [capacitance=10nF package="100 mil [THT, multilayer]"]
  R12 = Resistor [tolerance=±5% resistance=680 package=THT]
  R14 = Resistor [tolerance=±5% resistance=150 package=THT]
  P1 = Trimmer Potentiometer [maximum_resistance=500Ω package=THT]
  P2 = Trimmer Potentiometer [maximum_resistance=500Ω package=THT]
  R18 = Resistor [tolerance=±5% resistance=150 package=THT]
  T10 = PNP-Transistor [part_number=BC546B package="TO92 [THT]"]
  D3 = Rectifier Diode [part_number=1N4001 package="300 mil [THT]"]
  C3 = Ceramic Capacitor [capacitance=22nF package="100 mil [THT, multilayer]"]
  T3 = PNP-Transistor [part_number=BC556B package="TO92 [THT]"]
  R2 = Resistor [tolerance=±5% resistance=100 package=THT]
  R1 = Resistor [tolerance=±5% resistance=100 package=THT]
  T8 = NPN-Transistor [part_number=BC327 package="TO92 [THT]"]
  T2 = NPN-Transistor [part_number=BC546B package="TO92 [THT]"]
  T1 = NPN-Transistor [part_number=BC546B package="TO92 [THT]"]
  T5 = NPN-Transistor [part_number=BC546B package="TO92 [THT]"]
  R13 = Resistor [tolerance=±5% resistance=5.6k package=THT]
  R6 = Resistor [tolerance=±5% resistance=3.9k package=THT]
  Z1 = Zener Diode [part_number=1N4732A breakdown_voltage=9.1V package="300 mil [THT]"]
  D4 = Rectifier Diode [part_number=BZX84C10 package="300 mil [THT]"]
  V1_5V = Lilypad Power Supply
  V2_5V = Lilypad Power Supply
  RL2 = Resistor [tolerance=±5% resistance=10 package=THT]
  R16 = Resistor [tolerance=±5% resistance=10k package=THT]
  R15 = Resistor [tolerance=±5% resistance=68k package=THT]
  R17 = Resistor [tolerance=±5% resistance=2.2k package=THT]
  T6 = BF245 JFET N-Channel [part_number=J111 package=TO92]
  R3 = Resistor [tolerance=±5% resistance=10k package=THT]
  R8 = Resistor [tolerance=±5% resistance=4.7k package=THT]
  R7 = Resistor [tolerance=±5% resistance=15k package=THT]
  R9 = Resistor [tolerance=±5% resistance=10 package=THT]
  P3 = Trimmer Potentiometer [maximum_resistance=500kΩ package=THT]
  Cn4 = Ceramic Capacitor [capacitance=470nF package="100 mil [THT, multilayer]"]
  T7 = PNP-Transistor [part_number=BC556B package="TO92 [THT]"]
  D1 = Rectifier Diode [part_number=1N4148 package="300 mil [THT]"]
  R10 = Resistor [tolerance=±5% resistance=10 package=THT]
  RL1 = Resistor [tolerance=±5% resistance=10 package=THT]
  R11 = Resistor [tolerance=±5% resistance=1k package=THT]
  C4 = Ceramic Capacitor [capacitance=10nF package="100 mil [THT, multilayer]"]
  C2 = Ceramic Capacitor [capacitance=22nF package="100 mil [THT, multilayer]"]

nets (from the pcb view):
  N1: R5.Pin_0, P2.leg2
  N2: R5.Pin_1, LED2.anode, LED1.cathode, C5.0, V2_5V.+, RL2.Pin_1, C2.0
  N3: D2.cathode, C1.1, T8.B, T7.C
  N4: D2.anode, D3.cathode
  N5: R4.Pin_0, P1.leg2
  N6: R4.Pin_1, C3.1, C4.0
  N7: LED2.cathode, R14.Pin_0
  N8: C1.0, T3.C, T1.C, T7.B
  N9: T9.E, P1.leg1, P1.wiper, T8.E, R15.Pin_0, D1.cathode, R10.Pin_1
  N10: T9.B, T10.C, D3.anode
  N11: T9.C, R12.Pin_1, R14.Pin_1, R6.Pin_1, Z1.cathode, V2_5V.GND
  N12: LED1.anode, R18.Pin_1
  N13: T4.E, T2.C
  N14: T4.B, R3.Pin_0, R7.Pin_0
  N15: T4.C, R2.Pin_1
  N16: C5.1, P2.leg1, P2.wiper, C3.0, T1.B, C4.1, C2.1
  N17: R12.Pin_0, T10.E
  N18: R18.Pin_0, R2.Pin_0, R1.Pin_1, T8.C, D4.anode, V1_5V.+
  N19: T10.B, T5.B, R13.Pin_1, Z1.anode
  N20: T3.E, R1.Pin_0
  N21: T2.E, T1.E, T5.C
  N22: T5.E, R6.Pin_0
  N23: D4.cathode, T7.E
  N24: RL2.Pin_0, RL1.Pin_1
  N25: R16.Pin_0, R15.Pin_1
  N26: R16.Pin_1, R17.Pin_0
  N27: R17.Pin_1, RL1.Pin_0
  N28: T6.gate, R3.Pin_1
  N29: T6.source, P3.wiper
  N30: R8.Pin_0, R7.Pin_1
  N31: R8.Pin_1, R9.Pin_0
  N32: R9.Pin_1, R10.Pin_0
  N33: P3.leg1, Cn4.0
  N34: P3.leg2, Cn4.1, R11.Pin_0
  N35: D1.anode, R11.Pin_1

notes:
  Ground
  Vout

custom parts:
  BF245 JFET N-Channel: A BF245 JFET N-Channel Transistor
